// Logisim project Tarea1PabloAliaga.circ as structural Verilog: 2 circuits, main circuit main
module main (
  input  s,
  input  RESET,
  output x0,
  output x1,
  output x2,
  output d
);

  wire CLK_out, combinacional_1_d0, combinacional_1_d1, d0_q, d1_q, multiplexer_1_out, multiplexer_2_out;

  Clock CLK (.out(CLK_out));
  combinacional combinacional_1 (
    .s(s), .q0(d0_q), .q1(d1_q), .d0(combinacional_1_d0), .d1(combinacional_1_d1), .x0(x0), .x1(x1), .x2(x2),
    .d(d));
  D_Flip_Flop #(.trigger("falling")) d0 (
    .clk(CLK_out), .D(multiplexer_1_out), .Q(d0_q));  // open: Qn, preset, en, reset
  D_Flip_Flop #(.trigger("falling")) d1 (
    .clk(CLK_out), .D(multiplexer_2_out), .Q(d1_q));  // open: Qn, preset, en, reset
  Multiplexer multiplexer_1 (.in0(combinacional_1_d0), .in1(1'b0), .out(multiplexer_1_out), .sel(RESET));  // open: en
  Multiplexer multiplexer_2 (.in0(combinacional_1_d1), .in1(1'b0), .out(multiplexer_2_out), .sel(RESET));  // open: en

  // Notes on the sheet:
  //   CC4301|
  //   Entrega Tarea 1:
  //   por Pablo Aliaga
endmodule

// comb
module combinacional (
  input  s,
  input  q0,
  input  q1,
  output d0,
  output d1,
  output x0,
  output x1,
  output x2,
  output d
);

  wire and_1_out, and_2_out, and_3_out, not_1_out, not_2_out;

  not not_1 (not_1_out, s);
  not not_2 (not_2_out, q0);
  not not_3 (x0, q1);
  and and_1 (and_1_out, s, not_2_out, x0);
  and and_2 (and_2_out, not_1_out, q0, x0);
  and and_3 (and_3_out, s, q0);
  or or_1 (d0, and_1_out, and_2_out);
  and and_4 (d1, not_1_out, x0);
  and and_5 (x1, q1, q0);
  and and_6 (x2, s, q1);
  or or_2 (d, and_3_out, q1);
endmodule
