// Logisim project Tarea3PabloAliaga.circ as structural Verilog: 1 circuit, main circuit main
module main (
  input  STEP,
  input  CLK,
  output [7:0] PERIOD
);

  wire and_1_out, GUARDA_ESTADOS_q, not_1_out;
  wire [7:0] adder_1_out, CONTADOR_q, multiplexer_1_out;

  Multiplexer #(.width(8)) multiplexer_1 (
    .in0(adder_1_out), .in1(8'h1), .out(multiplexer_1_out), .sel(and_1_out));  // open: en
  and and_1 (and_1_out, STEP, not_1_out);
  Register #(.width(1), .trigger("falling")) GUARDA_ESTADOS (
    .D(STEP), .Q(GUARDA_ESTADOS_q), .clk(CLK));  // open: en, clr
  not not_1 (not_1_out, GUARDA_ESTADOS_q);
  Register #(.trigger("falling")) CONTADOR (.D(multiplexer_1_out), .Q(CONTADOR_q), .clk(CLK));  // open: en, clr
  Register #(.trigger("falling")) GUARDA_CONTEO_ANTERIOR (
    .D(CONTADOR_q), .en(and_1_out), .Q(PERIOD), .clk(CLK));  // open: clr
  Adder adder_1 (.a(CONTADOR_q), .b(8'h1), .out(adder_1_out));  // open: cin, cout

  // Notes on the sheet:
  //   Tarea 3
  //   Pablo Aliaga V.
endmodule
